# Fritzing sketch Control puramente pcb (saved by Fritzing 0.8.7b)
circuit board: 8.46667cm x 5.64444cm
breadboards: 1

parts:
  Power_plug1 = Power plug
  U1 = Voltage Regulator - 5V [package="TO220 [THT]"]
  U2 = 74HC595 [package="DIP16 [THT]"]
  U3 = 74HC595 [package="DIP16 [THT]"]
  C1 = Ceramic Capacitor [capacitance=100nF package="100 mil [THT, multilayer]"]
  C2 = Ceramic Capacitor [capacitance=100nF package="100 mil [THT, multilayer]"]
  Parte1 = Arduino Pro Mini v13
  IC1 = ULN2003A [package="DIP16 [THT]"]
  J1 = double row male pin header, 14 pins [form="♂ (male)"]
  J2 = male pin header, 4 pins [form="♂ (male)"]
  J3 = male pin header, 6 pins [form="♂ (male)"]

nets:
  N1: Power_plug1.VCC, U1.input_voltage, C1.0, Parte1.RAW
  N2: U1.GND, C2.0
  VCC: U1.output_voltage, U2.VCC, U3.VCC, C2.1, IC1.COM_-_Common, J1.pin7
  N3: U2.Q1, J1.pin3
  N4: U2.Q2, J1.pin4
  N5: U2.Q3, J1.pin5
  N6: U2.Q4, J2.pin1
  N7: U2.Q5, J2.pin2
  N8: U2.Q6, J2.pin3
  N9: U2.MR, U3.MR
  N10: U2.SH_CP, U3.SH_CP, Parte1.D3_PWM
  N11: U2.ST_CP, U3.ST_CP, Parte1.D4
  N12: U2.DS, U3.Q7'
  N13: U2.Q0, J1.pin2
  N14: U3.Q1, IC1.In_2
  N15: U3.Q2, IC1.In_3
  N16: U3.Q3, IC1.In_4
  N17: U3.Q4, IC1.In_5
  N18: U3.Q5, IC1.In_6
  N19: U3.Q6, IC1.In_7
  N20: U3.Q7, J1.pin1
  N21: U3.DS, Parte1.D2
  N22: U3.Q0, IC1.In_1
  N23: Parte1.DTR, J3.pin6
  N24: Parte1.D0/TX, J3.pin5
  N25: Parte1.D1/RX, J3.pin4
  N26: Parte1.VCC, J3.pin3
  N27: Parte1.GND, J3.pin1, J3.pin2
  N28: IC1.Out_7, J1.pin8
  N29: IC1.Out_6, J1.pin9
  N30: IC1.Out_5, J1.pin10
  N31: IC1.Out_4, J1.pin11
  N32: IC1.Out_3, J1.pin12
  N33: IC1.Out_2, J1.pin13
  N34: IC1.Out_1, J1.pin14
