# Fritzing sketch Display (saved by Fritzing 0.8.7b)
breadboards: 1

parts:
  ledA = LED - 5mm [color="Red (633nm)" package="5 mm [THT]"]
  R1 = Resistor [tolerance=±5% resistance=180 power=0.25W package=THT]
  ledA_2 = LED - 5mm [color="Red (633nm)" package="5 mm [THT]"]
  R2 = Resistor [tolerance=±5% resistance=180 power=0.25W package=THT]
  ledA_3 = LED - 5mm [color="Red (633nm)" package="5 mm [THT]"]
  R3 = Resistor [tolerance=±5% resistance=180 power=0.25W package=THT]
  ledA_4 = LED - 5mm [color="Red (633nm)" package="5 mm [THT]"]
  ledA_5 = LED - 5mm [color="Red (633nm)" package="5 mm [THT]"]
  R4 = Resistor [tolerance=±5% resistance=180 power=0.25W package=THT]
  R5 = Resistor [tolerance=±5% resistance=180 power=0.25W package=THT]
  ledB = LED - 5mm [color="Red (633nm)" package="5 mm [THT]"]
  ledB_2 = LED - 5mm [color="Red (633nm)" package="5 mm [THT]"]
  ledB_3 = LED - 5mm [color="Red (633nm)" package="5 mm [THT]"]
  ledB_4 = LED - 5mm [color="Red (633nm)" package="5 mm [THT]"]
  ledB_5 = LED - 5mm [color="Red (633nm)" package="5 mm [THT]"]
  R6 = Resistor [tolerance=±5% resistance=180 power=0.25W package=THT]
  R7 = Resistor [tolerance=±5% resistance=180 power=0.25W package=THT]
  R8 = Resistor [tolerance=±5% resistance=180 power=0.25W package=THT]
  R9 = Resistor [tolerance=±5% resistance=180 power=0.25W package=THT]
  R10 = Resistor [tolerance=±5% resistance=180 power=0.25W package=THT]
  ledG = LED - 5mm [color="Red (633nm)" package="5 mm [THT]"]
  ledG_2 = LED - 5mm [color="Red (633nm)" package="5 mm [THT]"]
  ledG_3 = LED - 5mm [color="Red (633nm)" package="5 mm [THT]"]
  ledG_4 = LED - 5mm [color="Red (633nm)" package="5 mm [THT]"]
  ledG_5 = LED - 5mm [color="Red (633nm)" package="5 mm [THT]"]
  R11 = Resistor [tolerance=±5% resistance=180 power=0.25W package=THT]
  R12 = Resistor [tolerance=±5% resistance=180 power=0.25W package=THT]
  R13 = Resistor [tolerance=±5% resistance=180 power=0.25W package=THT]
  R14 = Resistor [tolerance=±5% resistance=180 power=0.25W package=THT]
  R15 = Resistor [tolerance=±5% resistance=180 power=0.25W package=THT]
  ledC = LED - 5mm [color="Red (633nm)" package="5 mm [THT]"]
  ledC_2 = LED - 5mm [color="Red (633nm)" package="5 mm [THT]"]
  ledC_3 = LED - 5mm [color="Red (633nm)" package="5 mm [THT]"]
  ledC_4 = LED - 5mm [color="Red (633nm)" package="5 mm [THT]"]
  ledC_5 = LED - 5mm [color="Red (633nm)" package="5 mm [THT]"]
  R16 = Resistor [tolerance=±5% resistance=180 power=0.25W package=THT]
  R17 = Resistor [tolerance=±5% resistance=180 power=0.25W package=THT]
  R18 = Resistor [tolerance=±5% resistance=180 power=0.25W package=THT]
  R19 = Resistor [tolerance=±5% resistance=180 power=0.25W package=THT]
  R20 = Resistor [tolerance=±5% resistance=180 power=0.25W package=THT]
  ledE = LED - 5mm [color="Red (633nm)" package="5 mm [THT]"]
  ledF = LED - 5mm [color="Red (633nm)" package="5 mm [THT]"]
  ledE_2 = LED - 5mm [color="Red (633nm)" package="5 mm [THT]"]
  ledF_2 = LED - 5mm [color="Red (633nm)" package="5 mm [THT]"]
  ledE_3 = LED - 5mm [color="Red (633nm)" package="5 mm [THT]"]
  ledE_4 = LED - 5mm [color="Red (633nm)" package="5 mm [THT]"]
  ledF_3 = LED - 5mm [color="Red (633nm)" package="5 mm [THT]"]
  ledE_5 = LED - 5mm [color="Red (633nm)" package="5 mm [THT]"]
  ledF_4 = LED - 5mm [color="Red (633nm)" package="5 mm [THT]"]
  ledF_5 = LED - 5mm [color="Red (633nm)" package="5 mm [THT]"]
  R21 = Resistor [tolerance=±5% resistance=180 power=0.25W package=THT]
  R22 = Resistor [tolerance=±5% resistance=180 power=0.25W package=THT]
  R23 = Resistor [tolerance=±5% resistance=180 power=0.25W package=THT]
  R24 = Resistor [tolerance=±5% resistance=180 power=0.25W package=THT]
  R25 = Resistor [tolerance=±5% resistance=180 power=0.25W package=THT]
  R26 = Resistor [tolerance=±5% resistance=180 power=0.25W package=THT]
  R27 = Resistor [tolerance=±5% resistance=180 power=0.25W package=THT]
  R28 = Resistor [tolerance=±5% resistance=180 power=0.25W package=THT]
  R29 = Resistor [tolerance=±5% resistance=180 power=0.25W package=THT]
  R30 = Resistor [tolerance=±5% resistance=180 power=0.25W package=THT]
  ledD = LED - 5mm [color="Red (633nm)" package="5 mm [THT]"]
  ledD_2 = LED - 5mm [color="Red (633nm)" package="5 mm [THT]"]
  ledD_3 = LED - 5mm [color="Red (633nm)" package="5 mm [THT]"]
  ledD_4 = LED - 5mm [color="Red (633nm)" package="5 mm [THT]"]
  ledD_5 = LED - 5mm [color="Red (633nm)" package="5 mm [THT]"]
  R31 = Resistor [tolerance=±5% resistance=180 power=0.25W package=THT]
  R32 = Resistor [tolerance=±5% resistance=180 power=0.25W package=THT]
  R33 = Resistor [tolerance=±5% resistance=180 power=0.25W package=THT]
  R34 = Resistor [tolerance=±5% resistance=180 power=0.25W package=THT]
  R35 = Resistor [tolerance=±5% resistance=180 power=0.25W package=THT]

nets:
  N1: ledA.cathode, ledA_2.cathode, ledA_3.cathode, ledA_4.cathode, ledA_5.cathode
  N2: ledA.anode, R1.Pin_1
  N3: R1.Pin_0, R2.Pin_0, R3.Pin_0, R4.Pin_0, R5.Pin_0, R6.Pin_0, R7.Pin_0, R8.Pin_0, R9.Pin_0, R10.Pin_0, R11.Pin_0, R12.Pin_0, R13.Pin_0, R14.Pin_0, R15.Pin_0, R16.Pin_0, R17.Pin_0, R18.Pin_0, R19.Pin_0, R20.Pin_0, R21.Pin_0, R22.Pin_0, R23.Pin_0, R24.Pin_0, R25.Pin_0, R26.Pin_0, R27.Pin_0, R28.Pin_0, R29.Pin_0, R30.Pin_0, R31.Pin_0, R32.Pin_0, R33.Pin_0, R34.Pin_0, R35.Pin_0
  N4: ledA_2.anode, R2.Pin_1
  N5: ledA_3.anode, R3.Pin_1
  N6: ledA_4.anode, R4.Pin_1
  N7: ledA_5.anode, R5.Pin_1
  N8: ledB.cathode, ledB_2.cathode, ledB_3.cathode, ledB_4.cathode, ledB_5.cathode
  N9: ledB.anode, R6.Pin_1
  N10: ledB_2.anode, R9.Pin_1
  N11: ledB_3.anode, R8.Pin_1
  N12: ledB_4.anode, R10.Pin_1
  N13: ledB_5.anode, R7.Pin_1
  N14: ledG.cathode, ledG_2.cathode, ledG_3.cathode, ledG_4.cathode, ledG_5.cathode
  N15: ledG.anode, R11.Pin_1
  N16: ledG_2.anode, R14.Pin_1
  N17: ledG_3.anode, R13.Pin_1
  N18: ledG_4.anode, R15.Pin_1
  N19: ledG_5.anode, R12.Pin_1
  N20: ledC.cathode, ledC_2.cathode, ledC_3.cathode, ledC_4.cathode, ledC_5.cathode
  N21: ledC.anode, R18.Pin_1
  N22: ledC_2.anode, R19.Pin_1
  N23: ledC_3.anode, R20.Pin_1
  N24: ledC_4.anode, R17.Pin_1
  N25: ledC_5.anode, R16.Pin_1
  N26: ledE.cathode, ledE_2.cathode, ledE_3.cathode, ledE_4.cathode, ledE_5.cathode
  N27: ledE.anode, R27.Pin_1
  N28: ledF.cathode, ledF_2.cathode, ledF_3.cathode, ledF_4.cathode, ledF_5.cathode
  N29: ledF.anode, R22.Pin_1
  N30: ledE_2.anode, R24.Pin_1
  N31: ledF_2.anode, R29.Pin_1
  N32: ledE_3.anode, R25.Pin_1
  N33: ledE_4.anode, R30.Pin_1
  N34: ledF_3.anode, R23.Pin_1
  N35: ledE_5.anode, R28.Pin_1
  N36: ledF_4.anode, R21.Pin_1
  N37: ledF_5.anode, R26.Pin_1
  N38: ledD.cathode, ledD_2.cathode, ledD_3.cathode, ledD_4.cathode, ledD_5.cathode
  N39: ledD.anode, R32.Pin_1
  N40: ledD_2.anode, R33.Pin_1
  N41: ledD_3.anode, R34.Pin_1
  N42: ledD_4.anode, R31.Pin_1
  N43: ledD_5.anode, R35.Pin_1
