# Fritzing sketch display especial puramente pcb (saved by Fritzing 0.8.7b)
circuit board: 3.92007cm x 11cm
breadboards: 1

parts:
  LED6 = LED - 5mm [color="Red (633nm)" package="5 mm [THT]"]
  LED7 = LED - 5mm [color="Red (633nm)" package="5 mm [THT]"]
  LED8 = LED - 5mm [color="Red (633nm)" package="5 mm [THT]"]
  LED9 = LED - 5mm [color="Red (633nm)" package="5 mm [THT]"]
  LED10 = LED - 5mm [color="Red (633nm)" package="5 mm [THT]"]
  LED11 = LED - 5mm [color="Red (633nm)" package="5 mm [THT]"]
  LED12 = LED - 5mm [color="Red (633nm)" package="5 mm [THT]"]
  LED13 = LED - 5mm [color="Red (633nm)" package="5 mm [THT]"]
  LED14 = LED - 5mm [color="Red (633nm)" package="5 mm [THT]"]
  LED15 = LED - 5mm [color="Red (633nm)" package="5 mm [THT]"]
  R17 = Resistor [tolerance=±5% resistance=220 package=THT]
  R19 = Resistor [tolerance=±5% resistance=220 package=THT]
  R20 = Resistor [tolerance=±5% resistance=220 package=THT]
  R22 = Resistor [tolerance=±5% resistance=220 package=THT]
  R33 = Resistor [tolerance=±5% resistance=220 package=THT]
  R35 = Resistor [tolerance=±5% resistance=220 package=THT]
  R36 = Resistor [tolerance=±5% resistance=220 package=THT]
  R39 = Resistor [tolerance=±5% resistance=220 package=THT]
  R41 = Resistor [tolerance=±5% resistance=220 package=THT]
  Q1 = NPN-Transistor [package="TO92 [THT]"]
  R52 = Resistor [tolerance=±5% resistance=220 package=THT]
  J3 = female pin header, 1 pin [form="♀ (female)"]
  R53 = Resistor [tolerance=±5% resistance=220 package=THT]
  J2 = male pin header, 4 pins [form="♂ (male)"]

nets:
  N1: LED6.cathode, R36.Pin_1
  N2: LED6.anode, LED7.anode, LED8.anode, LED9.anode, LED10.anode, J2.pin2
  N3: LED7.cathode, R33.Pin_0
  N4: LED8.cathode, R41.Pin_1
  N5: LED9.cathode, R39.Pin_1
  N6: LED10.cathode, R35.Pin_1
  N7: LED11.cathode, R19.Pin_1
  N8: LED11.anode, LED12.anode, LED13.anode, LED14.anode, LED15.anode, J2.pin1
  N9: LED12.cathode, R22.Pin_0
  N10: LED13.cathode, R53.Pin_1
  N11: LED14.cathode, R17.Pin_1
  N12: LED15.cathode, R20.Pin_1
  N13: R17.Pin_0, R19.Pin_0, R20.Pin_0, R22.Pin_1, R33.Pin_1, R35.Pin_0, R36.Pin_0, R39.Pin_0, R41.Pin_0, Q1.E, R53.Pin_0
  N14: Q1.B, R52.Pin_1
  N15: Q1.C, J2.pin4
  N16: R52.Pin_0, J3.pin1
