# Fritzing sketch display puramente pcb (saved by Fritzing 0.8.7b)
circuit board: 7.5cm x 11cm
breadboards: 1

parts:
  LED1 = LED - 5mm [color="Red (633nm)" package="5 mm [THT]"]
  LED2 = LED - 5mm [color="Red (633nm)" package="5 mm [THT]"]
  LED3 = LED - 5mm [color="Red (633nm)" package="5 mm [THT]"]
  LED4 = LED - 5mm [color="Red (633nm)" package="5 mm [THT]"]
  LED5 = LED - 5mm [color="Red (633nm)" package="5 mm [THT]"]
  LED6 = LED - 5mm [color="Red (633nm)" package="5 mm [THT]"]
  LED7 = LED - 5mm [color="Red (633nm)" package="5 mm [THT]"]
  LED8 = LED - 5mm [color="Red (633nm)" package="5 mm [THT]"]
  LED9 = LED - 5mm [color="Red (633nm)" package="5 mm [THT]"]
  LED10 = LED - 5mm [color="Red (633nm)" package="5 mm [THT]"]
  LED11 = LED - 5mm [color="Red (633nm)" package="5 mm [THT]"]
  LED12 = LED - 5mm [color="Red (633nm)" package="5 mm [THT]"]
  LED13 = LED - 5mm [color="Red (633nm)" package="5 mm [THT]"]
  LED14 = LED - 5mm [color="Red (633nm)" package="5 mm [THT]"]
  LED15 = LED - 5mm [color="Red (633nm)" package="5 mm [THT]"]
  LED16 = LED - 5mm [color="Red (633nm)" package="5 mm [THT]"]
  LED17 = LED - 5mm [color="Red (633nm)" package="5 mm [THT]"]
  LED18 = LED - 5mm [color="Red (633nm)" package="5 mm [THT]"]
  LED19 = LED - 5mm [color="Red (633nm)" package="5 mm [THT]"]
  LED20 = LED - 5mm [color="Red (633nm)" package="5 mm [THT]"]
  LED21 = LED - 5mm [color="Red (633nm)" package="5 mm [THT]"]
  LED22 = LED - 5mm [color="Red (633nm)" package="5 mm [THT]"]
  LED23 = LED - 5mm [color="Red (633nm)" package="5 mm [THT]"]
  LED24 = LED - 5mm [color="Red (633nm)" package="5 mm [THT]"]
  LED25 = LED - 5mm [color="Red (633nm)" package="5 mm [THT]"]
  LED26 = LED - 5mm [color="Red (633nm)" package="5 mm [THT]"]
  LED27 = LED - 5mm [color="Red (633nm)" package="5 mm [THT]"]
  LED28 = LED - 5mm [color="Red (633nm)" package="5 mm [THT]"]
  LED29 = LED - 5mm [color="Red (633nm)" package="5 mm [THT]"]
  LED30 = LED - 5mm [color="Red (633nm)" package="5 mm [THT]"]
  LED31 = LED - 5mm [color="Red (633nm)" package="5 mm [THT]"]
  LED32 = LED - 5mm [color="Red (633nm)" package="5 mm [THT]"]
  LED33 = LED - 5mm [color="Red (633nm)" package="5 mm [THT]"]
  LED34 = LED - 5mm [color="Red (633nm)" package="5 mm [THT]"]
  LED35 = LED - 5mm [color="Red (633nm)" package="5 mm [THT]"]
  R11 = Resistor [tolerance=±5% resistance=220 package=THT]
  R12 = Resistor [tolerance=±5% resistance=220 package=THT]
  R13 = Resistor [tolerance=±5% resistance=220 package=THT]
  R14 = Resistor [tolerance=±5% resistance=220 package=THT]
  R15 = Resistor [tolerance=±5% resistance=220 package=THT]
  R16 = Resistor [tolerance=±5% resistance=220 package=THT]
  R17 = Resistor [tolerance=±5% resistance=220 package=THT]
  R19 = Resistor [tolerance=±5% resistance=220 package=THT]
  R20 = Resistor [tolerance=±5% resistance=220 package=THT]
  R21 = Resistor [tolerance=±5% resistance=220 package=THT]
  R22 = Resistor [tolerance=±5% resistance=220 package=THT]
  R23 = Resistor [tolerance=±5% resistance=220 package=THT]
  R24 = Resistor [tolerance=±5% resistance=220 package=THT]
  R25 = Resistor [tolerance=±5% resistance=220 package=THT]
  R26 = Resistor [tolerance=±5% resistance=220 package=THT]
  R27 = Resistor [tolerance=±5% resistance=220 package=THT]
  R28 = Resistor [tolerance=±5% resistance=220 package=THT]
  R29 = Resistor [tolerance=±5% resistance=220 package=THT]
  R30 = Resistor [tolerance=±5% resistance=220 package=THT]
  R31 = Resistor [tolerance=±5% resistance=220 package=THT]
  R32 = Resistor [tolerance=±5% resistance=220 package=THT]
  R33 = Resistor [tolerance=±5% resistance=220 package=THT]
  R35 = Resistor [tolerance=±5% resistance=220 package=THT]
  R36 = Resistor [tolerance=±5% resistance=220 package=THT]
  R37 = Resistor [tolerance=±5% resistance=220 package=THT]
  R39 = Resistor [tolerance=±5% resistance=220 package=THT]
  R41 = Resistor [tolerance=±5% resistance=220 package=THT]
  R42 = Resistor [tolerance=±5% resistance=220 package=THT]
  R43 = Resistor [tolerance=±5% resistance=220 package=THT]
  R44 = Resistor [tolerance=±5% resistance=220 package=THT]
  R45 = Resistor [tolerance=±5% resistance=220 package=THT]
  R46 = Resistor [tolerance=±5% resistance=220 package=THT]
  R49 = Resistor [tolerance=±5% resistance=220 package=THT]
  R50 = Resistor [tolerance=±5% resistance=220 package=THT]
  R51 = Resistor [tolerance=±5% resistance=220 package=THT]
  J1 = male pin header, 8 pins [form="♂ (male)"]
  Q1 = NPN-Transistor [package="TO92 [THT]"]
  R52 = Resistor [tolerance=±5% resistance=220 package=THT]
  J2 = male pin header, 8 pins [form="♂ (male)"]
  J3 = female pin header, 1 pin [form="♀ (female)"]

nets:
  N1: LED1.cathode, LED2.cathode, LED3.cathode, LED4.cathode, LED5.cathode, J2.pin7
  N2: LED1.anode, R37.Pin_0
  N3: LED2.anode, R42.Pin_1
  N4: LED3.anode, R32.Pin_1
  N5: LED4.anode, R43.Pin_1
  N6: LED5.anode, R49.Pin_1
  N7: LED6.cathode, R36.Pin_1
  N8: LED6.anode, LED7.anode, LED8.anode, LED9.anode, LED10.anode, J2.pin6
  N9: LED7.cathode, R33.Pin_0
  N10: LED8.cathode, R41.Pin_1
  N11: LED9.cathode, R39.Pin_1
  N12: LED10.cathode, R35.Pin_1
  N13: LED11.cathode, R19.Pin_1
  N14: LED11.anode, LED12.anode, LED13.anode, LED14.anode, LED15.anode, J2.pin5
  N15: LED12.cathode, R22.Pin_0
  N16: LED13.cathode, R16.Pin_1
  N17: LED14.cathode, R17.Pin_1
  N18: LED15.cathode, R20.Pin_1
  N19: LED16.cathode, LED17.cathode, LED18.cathode, LED19.cathode, LED20.cathode, J1.pin1
  N20: LED16.anode, R31.Pin_1
  N21: LED17.anode, R27.Pin_0
  N22: LED18.anode, R29.Pin_1
  N23: LED19.anode, R28.Pin_1
  N24: LED20.anode, R30.Pin_1
  N25: LED21.cathode, R26.Pin_0
  N26: LED21.anode, LED22.anode, LED23.anode, LED24.anode, LED25.anode, J2.pin4
  N27: LED22.cathode, R21.Pin_0
  N28: LED23.cathode, R24.Pin_0
  N29: LED24.cathode, R23.Pin_0
  N30: LED25.cathode, R25.Pin_0
  N31: LED26.cathode, R15.Pin_0
  N32: LED26.anode, LED27.anode, LED29.anode, LED31.anode, LED34.anode, J1.pin3
  N33: LED27.cathode, R12.Pin_0
  N34: LED28.cathode, R50.Pin_0
  N35: LED28.anode, LED30.anode, LED32.anode, LED33.anode, LED35.anode, J1.pin2
  N36: LED29.cathode, R11.Pin_0
  N37: LED30.cathode, R45.Pin_0
  N38: LED31.cathode, R13.Pin_0
  N39: LED32.cathode, R51.Pin_0
  N40: LED33.cathode, R46.Pin_0
  N41: LED34.cathode, R14.Pin_0
  N42: LED35.cathode, R44.Pin_0
  N43: R11.Pin_1, R12.Pin_1, R13.Pin_1, R14.Pin_1, R15.Pin_1, R16.Pin_0, R17.Pin_0, R19.Pin_0, R20.Pin_0, R21.Pin_1, R22.Pin_1, R23.Pin_1, R24.Pin_1, R25.Pin_1, R26.Pin_1, R27.Pin_1, R28.Pin_0, R29.Pin_0, R30.Pin_0, R31.Pin_0, R32.Pin_0, R33.Pin_1, R35.Pin_0, R36.Pin_0, R37.Pin_1, R39.Pin_0, R41.Pin_0, R42.Pin_0, R43.Pin_0, R44.Pin_1, R45.Pin_1, R46.Pin_1, R49.Pin_0, R50.Pin_1, R51.Pin_1, Q1.E
  N44: J1.pin8, Q1.C, J2.pin8
  N45: Q1.B, R52.Pin_1
  N46: R52.Pin_0, J3.pin1
