// Logisim project logica.circ as structural Verilog
module display (
  input  _1,
  input  _2,
  input  _3,
  input  _4,
  input  _5,
  input  _6,
  input  _7,
  input  _8,
  input  _9,
  input  _10,
  input  _11,
  input  _12,
  input  _13,
  input  _14,
  input  _15,
  input  _16
);

  wire and_1_out, and_2_out, and_3_out, and_4_out, and_5_out, and_6_out, and_7_out, and_8_out, and_9_out,
       and_10_out, and_11_out, and_12_out, and_13_out, and_14_out, and_15_out, and_16_out, and_17_out,
       and_18_out, and_19_out, and_20_out, and_21_out, and_22_out, and_23_out, and_24_out, and_25_out,
       and_26_out, and_27_out, and_28_out, and_29_out, undriven, undriven_2;

  LED led_1 (.in(undriven));
  LED led_2 (.in(undriven));
  LED led_3 (.in(undriven));
  LED led_4 (.in(undriven));
  LED led_5 (.in(undriven));
  LED led_6 (.in(undriven_2));
  LED led_7 (.in(undriven_2));
  LED led_8 (.in(undriven_2));
  LED led_9 (.in(undriven_2));
  LED led_10 (.in(undriven_2));
  LED led_11 (.in(and_3_out));
  LED led_12 (.in(and_3_out));
  LED led_13 (.in(and_3_out));
  and and_1 (and_1_out, _5, _12);
  LED led_14 (.in(and_3_out));
  LED led_15 (.in(and_1_out));
  LED led_16 (.in(and_3_out));
  LED led_17 (.in(and_5_out));
  LED led_18 (.in(and_5_out));
  LED led_19 (.in(and_1_out));
  LED led_20 (.in(and_5_out));
  LED led_21 (.in(and_5_out));
  LED led_22 (.in(and_5_out));
  LED led_23 (.in(and_2_out));
  LED led_24 (.in(and_2_out));
  LED led_25 (.in(and_2_out));
  and and_2 (and_2_out, _3, _9);
  and and_3 (and_3_out, _9, _6);
  and and_4 (and_4_out, _2, _9);
  LED led_26 (.in(and_4_out));
  LED led_27 (.in(and_4_out));
  LED led_28 (.in(and_4_out));
  and and_5 (and_5_out, _9, _13);
  and and_6 (and_6_out, _11, _9);
  LED led_29 (.in(and_6_out));
  LED led_30 (.in(and_6_out));
  LED led_31 (.in(and_6_out));
  LED led_32 (.in(and_2_out));
  LED led_33 (.in(and_2_out));
  LED led_34 (.in(and_7_out));
  LED led_35 (.in(and_7_out));
  LED led_36 (.in(and_7_out));
  and and_7 (and_7_out, _9, _1);
  LED led_37 (.in(and_7_out));
  LED led_38 (.in(and_7_out));
  LED led_39 (.in(and_4_out));
  LED led_40 (.in(and_4_out));
  LED led_41 (.in(and_8_out));
  LED led_42 (.in(and_8_out));
  LED led_43 (.in(and_8_out));
  and and_8 (and_8_out, _9, _4);
  LED led_44 (.in(and_8_out));
  LED led_45 (.in(and_8_out));
  LED led_46 (.in(and_6_out));
  LED led_47 (.in(and_6_out));
  LED led_48 (.in(and_12_out));
  LED led_49 (.in(and_12_out));
  LED led_50 (.in(and_9_out));
  LED led_51 (.in(and_9_out));
  LED led_52 (.in(and_9_out));
  and and_9 (and_9_out, _10, _6);
  LED led_53 (.in(and_9_out));
  LED led_54 (.in(and_9_out));
  and and_10 (and_10_out, _2, _10);
  LED led_55 (.in(and_10_out));
  LED led_56 (.in(and_10_out));
  LED led_57 (.in(and_11_out));
  LED led_58 (.in(and_11_out));
  LED led_59 (.in(and_11_out));
  and and_11 (and_11_out, _10, _13);
  LED led_60 (.in(and_11_out));
  LED led_61 (.in(and_11_out));
  LED led_62 (.in(and_15_out));
  LED led_63 (.in(and_15_out));
  LED led_64 (.in(and_12_out));
  LED led_65 (.in(and_12_out));
  LED led_66 (.in(and_12_out));
  and and_12 (and_12_out, _3, _10);
  LED led_67 (.in(and_13_out));
  LED led_68 (.in(and_13_out));
  and and_13 (and_13_out, _10, _1);
  LED led_69 (.in(and_13_out));
  LED led_70 (.in(and_13_out));
  LED led_71 (.in(and_13_out));
  LED led_72 (.in(and_10_out));
  LED led_73 (.in(and_10_out));
  LED led_74 (.in(and_10_out));
  LED led_75 (.in(and_14_out));
  LED led_76 (.in(and_14_out));
  and and_14 (and_14_out, _10, _4);
  LED led_77 (.in(and_14_out));
  LED led_78 (.in(and_14_out));
  LED led_79 (.in(and_14_out));
  and and_15 (and_15_out, _11, _10);
  LED led_80 (.in(and_15_out));
  LED led_81 (.in(and_15_out));
  LED led_82 (.in(and_15_out));
  LED led_83 (.in(and_1_out));
  LED led_84 (.in(and_1_out));
  LED led_85 (.in(and_19_out));
  LED led_86 (.in(and_19_out));
  LED led_87 (.in(and_16_out));
  LED led_88 (.in(and_16_out));
  LED led_89 (.in(and_16_out));
  and and_16 (and_16_out, _14, _6);
  LED led_90 (.in(and_16_out));
  and and_17 (and_17_out, _2, _14);
  LED led_91 (.in(and_16_out));
  LED led_92 (.in(and_17_out));
  LED led_93 (.in(and_17_out));
  LED led_94 (.in(and_18_out));
  LED led_95 (.in(and_18_out));
  LED led_96 (.in(and_18_out));
  and and_18 (and_18_out, _14, _13);
  LED led_97 (.in(and_18_out));
  LED led_98 (.in(and_18_out));
  LED led_99 (.in(and_22_out));
  LED led_100 (.in(and_22_out));
  LED led_101 (.in(and_19_out));
  LED led_102 (.in(and_19_out));
  LED led_103 (.in(and_19_out));
  and and_19 (and_19_out, _3, _14);
  LED led_104 (.in(and_20_out));
  LED led_105 (.in(and_20_out));
  and and_20 (and_20_out, _14, _1);
  LED led_106 (.in(and_20_out));
  LED led_107 (.in(and_20_out));
  LED led_108 (.in(and_20_out));
  LED led_109 (.in(and_17_out));
  LED led_110 (.in(and_17_out));
  LED led_111 (.in(and_17_out));
  LED led_112 (.in(and_21_out));
  LED led_113 (.in(and_21_out));
  LED led_114 (.in(and_21_out));
  and and_21 (and_21_out, _14, _4);
  LED led_115 (.in(and_21_out));
  LED led_116 (.in(and_21_out));
  and and_22 (and_22_out, _11, _14);
  LED led_117 (.in(and_22_out));
  LED led_118 (.in(and_22_out));
  LED led_119 (.in(and_22_out));
  LED led_120 (.in(and_26_out));
  LED led_121 (.in(and_23_out));
  LED led_122 (.in(and_23_out));
  LED led_123 (.in(and_23_out));
  and and_23 (and_23_out, _16, _6);
  LED led_124 (.in(and_23_out));
  and and_24 (and_24_out, _2, _16);
  LED led_125 (.in(and_23_out));
  LED led_126 (.in(and_24_out));
  LED led_127 (.in(and_25_out));
  LED led_128 (.in(and_25_out));
  LED led_129 (.in(and_25_out));
  and and_25 (and_25_out, _16, _13);
  LED led_130 (.in(and_25_out));
  LED led_131 (.in(and_25_out));
  LED led_132 (.in(and_29_out));
  LED led_133 (.in(and_26_out));
  LED led_134 (.in(and_26_out));
  LED led_135 (.in(and_26_out));
  LED led_136 (.in(and_26_out));
  and and_26 (and_26_out, _3, _16);
  and and_27 (and_27_out, _16, _1);
  LED led_137 (.in(and_24_out));
  LED led_138 (.in(and_24_out));
  LED led_139 (.in(and_24_out));
  LED led_140 (.in(and_24_out));
  and and_28 (and_28_out, _16, _4);
  and and_29 (and_29_out, _11, _16);
  LED led_141 (.in(and_29_out));
  LED led_142 (.in(and_29_out));
  LED led_143 (.in(and_29_out));
  LED led_144 (.in(and_29_out));
  LED led_145 (.in(and_27_out));
  LED led_146 (.in(and_27_out));
  LED led_147 (.in(and_27_out));
  LED led_148 (.in(and_27_out));
  LED led_149 (.in(and_27_out));
  LED led_150 (.in(and_28_out));
  LED led_151 (.in(and_28_out));
  LED led_152 (.in(and_28_out));
  LED led_153 (.in(and_28_out));
  LED led_154 (.in(and_28_out));
  LED led_155 ();  // open: in
  LED led_156 ();  // open: in
  LED led_157 ();  // open: in
endmodule

module conexiones (
  input  _1,
  input  _2,
  input  _3,
  input  _4,
  input  _5,
  input  _6,
  input  _7,
  input  _8,
  input  _9,
  input  _10,
  input  _11,
  input  _12,
  input  _13,
  input  _14,
  input  _15,
  input  _16
);
endmodule
