# Fritzing sketch modulo principal (saved by Fritzing 0.8.7b)
circuit board: 10.5cm x 5.2cm
breadboards: 1

parts:
  U1 = 74HC595 [package="DIP16 [THT]"]
  U2 = 74HC595 [package="DIP16 [THT]"]
  Power_plug1 = Power plug
  C1 = Ceramic Capacitor [capacitance=330nF voltage=10V package="100 mil [THT, multilayer]"]
  C2 = Ceramic Capacitor [capacitance=100nF package="100 mil [THT, multilayer]"]
  R7 = Resistor [tolerance=±5% resistance=180 package=THT]
  R8 = Resistor [tolerance=±5% resistance=180 package=THT]
  R9 = Resistor [tolerance=±5% resistance=180 package=THT]
  R10 = Resistor [tolerance=±5% resistance=180 package=THT]
  R11 = Resistor [tolerance=±5% resistance=180 package=THT]
  R12 = Resistor [tolerance=±5% resistance=180 package=THT]
  R13 = Resistor [tolerance=±5% resistance=180 package=THT]
  Q1 = NPN-Transistor [package="TO92 [THT]"]
  Q2 = NPN-Transistor [package="TO92 [THT]"]
  Q3 = NPN-Transistor [package="TO92 [THT]"]
  Q4 = NPN-Transistor [package="TO92 [THT]"]
  Q5 = NPN-Transistor [package="TO92 [THT]"]
  R14 = Resistor [tolerance=±5% resistance=180 package=THT]
  R15 = Resistor [tolerance=±5% resistance=180 package=THT]
  R16 = Resistor [tolerance=±5% resistance=180 package=THT]
  R17 = Resistor [tolerance=±5% resistance=180 package=THT]
  R18 = Resistor [tolerance=±5% resistance=180 package=THT]
  Q7 = NPN-Transistor [package="TO92 [THT]"]
  R19 = Resistor [tolerance=±10% resistance=1k package=THT]
  R20 = Resistor [tolerance=±5% resistance=10k package=THT]
  D1 = Rectifier Diode [part_number=1N4001 package="300 mil [THT]"]
  J3 = screw terminal, 4 pins
  R21 = Resistor [tolerance=±5% resistance=10k package=THT]
  Q9 = NPN-Transistor [package="TO92 [THT]"]
  R22 = Resistor [tolerance=±10% resistance=1k package=THT]
  R23 = Resistor [tolerance=±5% resistance=10k package=THT]
  D2 = Rectifier Diode [part_number=1N4001 package="300 mil [THT]"]
  R24 = Resistor [tolerance=±5% resistance=10k package=THT]
  Q11 = NPN-Transistor [package="TO92 [THT]"]
  R25 = Resistor [tolerance=±10% resistance=1k package=THT]
  R26 = Resistor [tolerance=±5% resistance=10k package=THT]
  D3 = Rectifier Diode [part_number=1N4001 package="300 mil [THT]"]
  R27 = Resistor [tolerance=±5% resistance=10k package=THT]
  J5 = male pin header, 4 pins [form="♂ (male)"]
  LED5 = LED - 3mm [color="Red (633nm)" package="3 mm [THT]"]
  LED4 = LED - 3mm [color="Red (633nm)" package="3 mm [THT]"]
  U4 = Voltage Regulator - 5V [package="TO220 [THT]"]
  J1 = female pin header, 8 pins [form="♀ (female)"]
  J2 = female pin header, 8 pins [form="♀ (female)"]
  LED7 = LED - 3mm [color="Red (633nm)" package="3 mm [THT]"]
  LED8 = LED - 3mm [color="Red (633nm)" package="3 mm [THT]"]
  U3 = SWITCH-SPST-2 [package=switch-spst-vertical]
  J4 = male pin header, 5 pins [form="♂ (male)"]
  Q6 = pnp-Powertransistor [package="TO220 [THT]"]
  Q8 = pnp-Powertransistor [package="TO220 [THT]"]
  Q10 = pnp-Powertransistor [package="TO220 [THT]"]
  Parte2 = Arduino Pro Mini v13

nets:
  N1: U1.Q1, R9.Pin_0
  N2: U1.Q2, R7.Pin_0
  N3: U1.Q3, R10.Pin_0
  N4: U1.Q4, R11.Pin_0
  N5: U1.Q5, R12.Pin_0
  N6: U1.Q6, R13.Pin_0
  N7: U1.Q7, R14.Pin_0
  GND: U1.GND, U1.OE, U2.GND, U2.OE, Power_plug1.GND, C1.0, C2.1, Q7.E, J3.pin1, Q9.E, Q11.E, J5.pin1, U4.GND, J4.pin1, Parte2.GND
  N8: U1.Q7', U2.DS
  VCC: U1.MR, U1.VCC, U2.MR, U2.VCC, C2.0, Q1.C, Q2.C, Q3.C, Q4.C, Q5.C, U4.output_voltage, J4.pin5, Parte2.VCC
  N9: U1.SH_CP, U2.SH_CP, Parte2.D3_PWM
  N10: U1.ST_CP, U2.ST_CP, Parte2.D4
  N11: U1.DS, Parte2.D2
  N12: U1.Q0, R8.Pin_0
  N13: U2.Q1, R16.Pin_0
  N14: U2.Q2, R18.Pin_0
  N15: U2.Q3, R15.Pin_0
  N16: U2.Q4, D1.anode, J5.pin4
  N17: U2.Q5, D2.anode, J5.pin3
  N18: U2.Q6, D3.anode, J5.pin2
  N19: U2.Q0, R17.Pin_0
  N20: Power_plug1.VCC, U3.P
  N21: C1.1, R21.Pin_1, R24.Pin_1, R27.Pin_1, U4.input_voltage, U3.O, Q6.emitter, Q8.emitter, Q10.emitter
  N22: R7.Pin_1, LED4.cathode, J1.pin4
  N23: R8.Pin_1, J1.pin3, J1.pin5, LED7.cathode, LED8.cathode
  N24: R9.Pin_1, LED5.cathode, J1.pin1
  N25: R10.Pin_1, J2.pin3
  N26: R11.Pin_1, J2.pin5
  N27: R12.Pin_1, J1.pin6
  N28: R13.Pin_1, J1.pin2
  N29: Q1.E, LED5.anode, LED4.anode, J2.pin4, LED7.anode, LED8.anode
  N30: Q1.B, R14.Pin_1
  N31: Q2.E, J2.pin1
  N32: Q2.B, R17.Pin_1
  N33: Q3.E, J2.pin2
  N34: Q3.B, R16.Pin_1
  N35: Q4.E, J2.pin6
  N36: Q4.B, R18.Pin_1
  N37: Q5.E, J2.pin8
  N38: Q5.B, R15.Pin_1
  N39: Q7.B, R20.Pin_1
  N40: Q7.C, R19.Pin_0, R21.Pin_0
  N41: R19.Pin_1, Q6.base
  N42: R20.Pin_0, D1.cathode
  N43: J3.pin2, Q10.collector
  N44: J3.pin3, Q8.collector
  N45: J3.pin4, Q6.collector
  N46: Q9.B, R23.Pin_1
  N47: Q9.C, R22.Pin_0, R24.Pin_0
  N48: R22.Pin_1, Q8.base
  N49: R23.Pin_0, D2.cathode
  N50: Q11.B, R26.Pin_1
  N51: Q11.C, R25.Pin_0, R27.Pin_0
  N52: R25.Pin_1, Q10.base
  N53: R26.Pin_0, D3.cathode
  N54: J4.pin2, Parte2.D7
  N55: J4.pin3, Parte2.D6_PWM
  N56: J4.pin4, Parte2.D5_PWM

custom parts:
  Arduino Pro Mini v13: It's blue! It's thin! It's the Arduino Pro Mini! SparkFun's minimal design approach to Arduino. This is a 5V Arduino running the 16MHz bootloader. Arduino Pro Mini does not come with connectors populated so that you can solder in any connector or wire with any orientation you need. We recommend first time Arduino users start with the Uno R3. It's a great board that will get you up and running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
