# Fritzing sketch botones (saved by Fritzing 0.8.7b)
circuit board: 6cm x 1.6cm

parts:
  S1 = Pushbutton [package="[THT]"]
  S2 = Pushbutton [package="[THT]"]
  S3 = Pushbutton [package="[THT]"]
  C1 = Ceramic Capacitor [capacitance=100nF package="100 mil [THT, multilayer]"]
  C2 = Ceramic Capacitor [capacitance=100nF package="100 mil [THT, multilayer]"]
  C3 = Ceramic Capacitor [capacitance=100nF package="100 mil [THT, multilayer]"]
  R1 = Resistor [tolerance=±10% resistance=10k package=THT]
  R2 = Resistor [tolerance=±10% resistance=10k package=THT]
  R3 = Resistor [tolerance=±10% resistance=10k package=THT]
  J1 = female pin header, 5 pins [form="♀ (female)"]

nets:
  N1: S1.Pin_1, S1.Pin_2, C1.0, R1.Pin_1, J1.pin4
  N2: S1.Pin_3, S1.Pin_4, S2.Pin_3, S2.Pin_4, S3.Pin_3, S3.Pin_4, C1.1, C2.1, C3.1, J1.pin5
  N3: S2.Pin_1, S2.Pin_2, C2.0, R2.Pin_1, J1.pin3
  N4: S3.Pin_1, S3.Pin_2, C3.0, R3.Pin_1, J1.pin2
  N5: R1.Pin_0, R2.Pin_0, R3.Pin_0, J1.pin1
