# Fritzing sketch leds (saved by Fritzing 0.8.7b)
circuit board: 1.5cm x 4cm

parts:
  R2 = Resistor [tolerance=±5% resistance=180 package=THT]
  R3 = Resistor [tolerance=±5% resistance=180 package=THT]
  R4 = Resistor [tolerance=±5% resistance=180 package=THT]
  LED1 = LED - 3mm [color="Red (633nm)" package="3 mm [THT]"]
  LED2 = LED - 3mm [color="Orange (620nm)" package="3 mm [THT]"]
  LED3 = LED - 3mm [color="Green (565nm)" package="3 mm [THT]"]
  J1 = female pin header, 4 pins [form="♀ (female)"]

nets:
  N1: R2.Pin_0, R3.Pin_0, R4.Pin_0, J1.pin1
  N2: R2.Pin_1, LED1.cathode
  N3: R3.Pin_1, LED2.cathode
  N4: R4.Pin_1, LED3.cathode
  N5: LED1.anode, J1.pin2
  N6: LED2.anode, J1.pin3
  N7: LED3.anode, J1.pin4
