# Fritzing sketch modulo principal_ground fill (saved by Fritzing 0.8.7b)
circuit board: 10.5cm x 5.2cm
breadboards: 1

parts:
  U1 = 74HC595 [package="DIP16 [THT]"]
  U2 = 74HC595 [package="DIP16 [THT]"]
  Power_plug1 = Power plug
  Parte1 = Arduino Pro Mini v13
  C1 = Ceramic Capacitor [capacitance=330nF voltage=10V package="100 mil [THT, multilayer]"]
  C2 = Ceramic Capacitor [capacitance=100nF package="100 mil [THT, multilayer]"]
  R7 = Resistor [tolerance=±5% resistance=180 package=THT]
  R8 = Resistor [tolerance=±5% resistance=180 package=THT]
  R9 = Resistor [tolerance=±5% resistance=180 package=THT]
  R10 = Resistor [tolerance=±5% resistance=180 package=THT]
  R11 = Resistor [tolerance=±5% resistance=180 package=THT]
  R12 = Resistor [tolerance=±5% resistance=180 package=THT]
  R13 = Resistor [tolerance=±5% resistance=180 package=THT]
  Q1 = NPN-Transistor [package="TO92 [THT]"]
  Q2 = NPN-Transistor [package="TO92 [THT]"]
  Q3 = NPN-Transistor [package="TO92 [THT]"]
  Q4 = NPN-Transistor [package="TO92 [THT]"]
  Q5 = NPN-Transistor [package="TO92 [THT]"]
  R14 = Resistor [tolerance=±5% resistance=180 package=THT]
  R15 = Resistor [tolerance=±5% resistance=180 package=THT]
  R16 = Resistor [tolerance=±5% resistance=180 package=THT]
  R17 = Resistor [tolerance=±5% resistance=180 package=THT]
  R18 = Resistor [tolerance=±5% resistance=180 package=THT]
  Q6 = PNP-Transistor [package="TO92 [THT]"]
  Q7 = NPN-Transistor [package="TO92 [THT]"]
  R19 = Resistor [tolerance=±10% resistance=1k package=THT]
  R20 = Resistor [tolerance=±5% resistance=10k package=THT]
  D1 = Rectifier Diode [part_number=1N4001 package="300 mil [THT]"]
  J3 = screw terminal, 4 pins
  R21 = Resistor [tolerance=±5% resistance=10k package=THT]
  Q8 = PNP-Transistor [package="TO92 [THT]"]
  Q9 = NPN-Transistor [package="TO92 [THT]"]
  R22 = Resistor [tolerance=±10% resistance=1k package=THT]
  R23 = Resistor [tolerance=±5% resistance=10k package=THT]
  D2 = Rectifier Diode [part_number=1N4001 package="300 mil [THT]"]
  R24 = Resistor [tolerance=±5% resistance=10k package=THT]
  Q10 = PNP-Transistor [package="TO92 [THT]"]
  Q11 = NPN-Transistor [package="TO92 [THT]"]
  R25 = Resistor [tolerance=±10% resistance=1k package=THT]
  R26 = Resistor [tolerance=±5% resistance=10k package=THT]
  D3 = Rectifier Diode [part_number=1N4001 package="300 mil [THT]"]
  R27 = Resistor [tolerance=±5% resistance=10k package=THT]
  J5 = male pin header, 4 pins [form="♂ (male)"]
  LED5 = LED - 3mm [color="Red (633nm)" package="3 mm [THT]"]
  LED4 = LED - 3mm [color="Red (633nm)" package="3 mm [THT]"]
  U4 = Voltage Regulator - 5V [package="TO220 [THT]"]
  J1 = female pin header, 8 pins [form="♀ (female)"]
  J2 = female pin header, 8 pins [form="♀ (female)"]
  LED7 = LED - 3mm [color="Red (633nm)" package="3 mm [THT]"]
  LED8 = LED - 3mm [color="Red (633nm)" package="3 mm [THT]"]
  U3 = SWITCH-SPST-2 [package=switch-spst-vertical]
  J4 = male pin header, 5 pins [form="♂ (male)"]

nets:
  N1: U1.Q1, R9.Pin_0
  N2: U1.Q2, R7.Pin_0
  N3: U1.Q3, R10.Pin_0
  N4: U1.Q4, R11.Pin_0
  N5: U1.Q5, R12.Pin_0
  N6: U1.Q6, R13.Pin_0
  N7: U1.Q7, R14.Pin_0
  GND: U1.GND, U1.OE, U2.GND, U2.OE, Power_plug1.GND, Parte1.GND, C1.0, C2.1, Q7.E, J3.pin1, Q9.E, Q11.E, J5.pin1, U4.GND, J4.pin1
  N8: U1.Q7', U2.DS
  VCC: U1.MR, U1.VCC, U2.MR, U2.VCC, Parte1.VCC, C2.0, Q1.C, Q2.C, Q3.C, Q4.C, Q5.C, U4.output_voltage, J4.pin5
  N9: U1.SH_CP, U2.SH_CP, Parte1.D3_PWM
  N10: U1.ST_CP, U2.ST_CP, Parte1.D4
  N11: U1.DS, Parte1.D2
  N12: U1.Q0, R8.Pin_0
  N13: U2.Q1, R16.Pin_0
  N14: U2.Q2, R18.Pin_0
  N15: U2.Q3, R15.Pin_0
  N16: U2.Q4, D1.anode, J5.pin4
  N17: U2.Q5, D2.anode, J5.pin3
  N18: U2.Q6, D3.anode, J5.pin2
  N19: U2.Q0, R17.Pin_0
  N20: Power_plug1.VCC, U3.P
  N21: Parte1.D7, J4.pin2
  N22: Parte1.D6_PWM, J4.pin3
  N23: Parte1.D5_PWM, J4.pin4
  N24: C1.1, Q6.E, R21.Pin_1, Q8.E, R24.Pin_1, Q10.E, R27.Pin_1, U4.input_voltage, U3.O
  N25: R7.Pin_1, LED4.cathode, J1.pin4
  N26: R8.Pin_1, J1.pin3, J1.pin5, LED7.cathode, LED8.cathode
  N27: R9.Pin_1, LED5.cathode, J1.pin1
  N28: R10.Pin_1, J2.pin3
  N29: R11.Pin_1, J2.pin5
  N30: R12.Pin_1, J1.pin6
  N31: R13.Pin_1, J1.pin2
  N32: Q1.E, LED5.anode, LED4.anode, J2.pin4, LED7.anode, LED8.anode
  N33: Q1.B, R14.Pin_1
  N34: Q2.E, J2.pin1
  N35: Q2.B, R17.Pin_1
  N36: Q3.E, J2.pin2
  N37: Q3.B, R16.Pin_1
  N38: Q4.E, J2.pin6
  N39: Q4.B, R18.Pin_1
  N40: Q5.E, J2.pin8
  N41: Q5.B, R15.Pin_1
  N42: Q6.B, R19.Pin_1
  N43: Q6.C, J3.pin4
  N44: Q7.B, R20.Pin_1
  N45: Q7.C, R19.Pin_0, R21.Pin_0
  N46: R20.Pin_0, D1.cathode
  N47: J3.pin2, Q10.C
  N48: J3.pin3, Q8.C
  N49: Q8.B, R22.Pin_1
  N50: Q9.B, R23.Pin_1
  N51: Q9.C, R22.Pin_0, R24.Pin_0
  N52: R23.Pin_0, D2.cathode
  N53: Q10.B, R25.Pin_1
  N54: Q11.B, R26.Pin_1
  N55: Q11.C, R25.Pin_0, R27.Pin_0
  N56: R26.Pin_0, D3.cathode
