# Fritzing sketch tablero (saved by Fritzing 0.8.7b)
breadboards: 1

parts:
  U1 = 74HC595 [package="DIP16 [THT]"]
  U2 = 74HC595 [package="DIP16 [THT]"]
  U3 = SWITCH-SPST-2 [package=switch-spst-vertical]
  S1 = Momentary Switch [package=ksa_sealed_tac_switch]
  S2 = Momentary Switch [package=ksa_sealed_tac_switch]
  S3 = Momentary Switch [package=ksa_sealed_tac_switch]
  Power_plug1 = Power plug
  Parte1 = Arduino Pro Mini v13
  U4 = Voltage Regulator - 5V [package="TO220 [THT]"]
  C1 = Ceramic Capacitor [capacitance=330nF voltage=10V package="100 mil [THT, multilayer]"]
  C2 = Ceramic Capacitor [capacitance=100nF package="100 mil [THT, multilayer]"]
  C3 = Ceramic Capacitor [capacitance=100nF package="100 mil [THT, multilayer]"]
  C4 = Ceramic Capacitor [capacitance=100nF package="100 mil [THT, multilayer]"]
  C5 = Ceramic Capacitor [capacitance=100nF package="100 mil [THT, multilayer]"]
  R1 = Resistor [tolerance=±5% resistance=10k package=THT]
  R2 = Resistor [tolerance=±5% resistance=10k package=THT]
  R3 = Resistor [tolerance=±10% resistance=10k package=THT]
  R4 = Resistor [tolerance=±5% resistance=180 package=THT]
  R5 = Resistor [tolerance=±5% resistance=180 package=THT]
  R6 = Resistor [tolerance=±5% resistance=180 package=THT]
  LED1 = LED - 5mm [color="Red (633nm)" package="5 mm [THT]"]
  LED2 = LED - 5mm [color="Green (570nm)" package="5 mm [THT]"]
  LED3 = smd LED [color="Orange (605nm)" package="0603 [SMD]"]
  J1 = male pin header, 8 pins [form="♂ (male)"]
  J2 = male pin header, 8 pins [form="♂ (male)"]
  R7 = Resistor [tolerance=±5% resistance=180 package=THT]
  R8 = Resistor [tolerance=±5% resistance=180 package=THT]
  R9 = Resistor [tolerance=±5% resistance=180 package=THT]
  R10 = Resistor [tolerance=±5% resistance=180 package=THT]
  R11 = Resistor [tolerance=±5% resistance=180 package=THT]
  R12 = Resistor [tolerance=±5% resistance=180 package=THT]
  R13 = Resistor [tolerance=±5% resistance=180 package=THT]
  Q1 = NPN-Transistor [package="TO92 [THT]"]
  Q2 = NPN-Transistor [package="TO92 [THT]"]
  Q3 = NPN-Transistor [package="TO92 [THT]"]
  Q4 = NPN-Transistor [package="TO92 [THT]"]
  Q5 = NPN-Transistor [package="TO92 [THT]"]
  R14 = Resistor [tolerance=±5% resistance=180 package=THT]
  R15 = Resistor [tolerance=±5% resistance=180 package=THT]
  R16 = Resistor [tolerance=±5% resistance=180 package=THT]
  R17 = Resistor [tolerance=±5% resistance=180 package=THT]
  R18 = Resistor [tolerance=±5% resistance=180 package=THT]
  LED4 = LED - 5mm [color="Red (633nm)" package="5 mm [THT]"]
  LED5 = LED - 5mm [color="Red (633nm)" package="5 mm [THT]"]
  Q6 = PNP-Transistor [package="TO92 [THT]"]
  Q7 = NPN-Transistor [package="TO92 [THT]"]
  R19 = Resistor [tolerance=±10% resistance=1k package=THT]
  R20 = Resistor [tolerance=±5% resistance=10k package=THT]
  D1 = Rectifier Diode [part_number=1N4001 package="300 mil [THT]"]
  J3 = screw terminal, 4 pins
  R21 = Resistor [tolerance=±5% resistance=10k package=THT]
  Q8 = PNP-Transistor [package="TO92 [THT]"]
  Q9 = NPN-Transistor [package="TO92 [THT]"]
  R22 = Resistor [tolerance=±10% resistance=1k package=THT]
  R23 = Resistor [tolerance=±5% resistance=10k package=THT]
  D2 = Rectifier Diode [part_number=1N4001 package="300 mil [THT]"]
  R24 = Resistor [tolerance=±5% resistance=10k package=THT]
  Q10 = PNP-Transistor [package="TO92 [THT]"]
  Q11 = NPN-Transistor [package="TO92 [THT]"]
  R25 = Resistor [tolerance=±10% resistance=1k package=THT]
  R26 = Resistor [tolerance=±5% resistance=10k package=THT]
  D3 = Rectifier Diode [part_number=1N4001 package="300 mil [THT]"]
  R27 = Resistor [tolerance=±5% resistance=10k package=THT]

nets:
  N1: U1.Q1, R9.Pin_0
  N2: U1.Q2, R7.Pin_0
  N3: U1.Q3, R10.Pin_0
  N4: U1.Q4, R11.Pin_0
  N5: U1.Q5, R12.Pin_0
  N6: U1.Q6, R13.Pin_0
  N7: U1.Q7, R14.Pin_0
  GND: U1.GND, U1.OE, U2.GND, U2.OE, Power_plug1.GND, Parte1.GND, U4.GND, C1.0, C2.1, R1.Pin_1, R2.Pin_1, R3.Pin_1, LED1.cathode, LED2.cathode, LED3.cathode, Q7.E, J3.pin1, Q9.E, Q11.E
  N8: U1.Q7', U2.DS
  VCC: U1.MR, U1.VCC, U2.MR, U2.VCC, U3.O, S1.1, S2.1, S3.1, Parte1.VCC, C3.1, C4.1, C5.1, Q1.C, Q2.C, Q3.C, Q4.C, Q5.C
  N9: U1.SH_CP, U2.SH_CP, Parte1.D3_PWM
  N10: U1.ST_CP, U2.ST_CP, Parte1.D4
  N11: U1.DS, Parte1.D2
  N12: U1.Q0, R8.Pin_0
  N13: U2.Q1, R16.Pin_0
  N14: U2.Q2, R18.Pin_0
  N15: U2.Q3, R15.Pin_0
  N16: U2.Q4, R6.Pin_0, D1.anode
  N17: U2.Q5, R4.Pin_0, D2.anode
  N18: U2.Q6, R5.Pin_0, D3.anode
  N19: U2.Q0, R17.Pin_0
  N20: U3.P, U4.output_voltage, C2.0
  N21: S1.3, Parte1.D5_PWM, C5.0, R1.Pin_0
  N22: S2.3, Parte1.D6_PWM, C4.0, R2.Pin_0
  N23: S3.3, Parte1.D7, C3.0, R3.Pin_0
  N24: Power_plug1.VCC, U4.input_voltage, C1.1, Q6.E, R21.Pin_1, Q8.E, R24.Pin_1, Q10.E, R27.Pin_1
  N25: R4.Pin_1, LED3.anode
  N26: R5.Pin_1, LED1.anode
  N27: R6.Pin_1, LED2.anode
  N28: J1.pin1, R9.Pin_1, LED5.cathode
  N29: J1.pin2, R13.Pin_1
  N30: J1.pin3, J1.pin5, R8.Pin_1
  N31: J1.pin4, R7.Pin_1, LED4.cathode
  N32: J1.pin6, R12.Pin_1
  N33: J2.pin1, Q2.E
  N34: J2.pin2, Q3.E
  N35: J2.pin3, R10.Pin_1
  N36: J2.pin4, Q1.E, LED4.anode, LED5.anode
  N37: J2.pin5, R11.Pin_1
  N38: J2.pin6, Q4.E
  N39: J2.pin8, Q5.E
  N40: Q1.B, R14.Pin_1
  N41: Q2.B, R17.Pin_1
  N42: Q3.B, R16.Pin_1
  N43: Q4.B, R18.Pin_1
  N44: Q5.B, R15.Pin_1
  N45: Q6.B, R19.Pin_1
  N46: Q6.C, J3.pin4
  N47: Q7.B, R20.Pin_1
  N48: Q7.C, R19.Pin_0, R21.Pin_0
  N49: R20.Pin_0, D1.cathode
  N50: J3.pin2, Q10.C
  N51: J3.pin3, Q8.C
  N52: Q8.B, R22.Pin_1
  N53: Q9.B, R23.Pin_1
  N54: Q9.C, R22.Pin_0, R24.Pin_0
  N55: R23.Pin_0, D2.cathode
  N56: Q10.B, R25.Pin_1
  N57: Q11.B, R26.Pin_1
  N58: Q11.C, R25.Pin_0, R27.Pin_0
  N59: R26.Pin_0, D3.cathode
