# Fritzing sketch nuevo tablero (saved by Fritzing 0.8.7b)
breadboards: 1

parts:
  U1 = 74HC595 [package="DIP16 [THT]"]
  U2 = 74HC595 [package="DIP16 [THT]"]
  U3 = SWITCH-SPST-2 [package=switch-spst-vertical]  # not connected
  S1 = Momentary Switch [package=ksa_sealed_tac_switch]  # not connected
  S2 = Momentary Switch [package=ksa_sealed_tac_switch]  # not connected
  S3 = Momentary Switch [package=ksa_sealed_tac_switch]  # not connected
  Power_plug1 = Power plug
  Parte1 = Arduino Pro Mini v13
  U4 = Voltage Regulator - 5V [package="TO220 [THT]"]
  C1 = Ceramic Capacitor [capacitance=100nF package="100 mil [THT, multilayer]"]
  C2 = Ceramic Capacitor [capacitance=100nF package="100 mil [THT, multilayer]"]
  Q1 = NPN-Transistor [package="TO92 [THT]"]  # not connected
  Q2 = NPN-Transistor [package="TO92 [THT]"]  # not connected
  Q3 = NPN-Transistor [package="TO92 [THT]"]  # not connected

nets:
  GND: U1.GND, U2.GND, Power_plug1.GND, Parte1.GND, U4.GND, C1.0, C2.1
  VCC: U1.VCC, U2.VCC
  N1: Power_plug1.VCC, U4.input_voltage, C1.1
  N2: Parte1.VCC, U4.output_voltage, C2.0
